# Fritzing sketch Nano_plus_W5500 (saved by Fritzing 0.9.4)

parts:
  Part1 = Arduino Nano (Rev3.0)
  W5500_Module1 = W5500 Ethernet module [package="DIP (Dual Inline) [THT]"]

nets:
  N1: Part1.D10, W5500_Module1.SCS
  N2: Part1.D11/MOSI, W5500_Module1.MOSI
  N3: Part1.D12/MISO, W5500_Module1.MISO
  GND: Part1.GND, W5500_Module1.GND
  N4: Part1.RESET, W5500_Module1.RST
  5V: Part1.5V, W5500_Module1.5V
  N5: Part1.D13/SCK, W5500_Module1.SCLK

custom parts:
  W5500 Ethernet module: W5500 based SPI Ethernet module for Arduino, etc.
